// Logisim project alu.circ as structural Verilog: 1 circuit, main circuit alu
module alu (
  input  [31:0] A,
  input  [31:0] B,
  input  [3:0] ALUSel,
  output [31:0] Result
);

  wire comparator_1_lt, m;
  wire [31:0] a1, add, b1, divu, mult, multhu, multiplexer_4_out, multiplier_2_cout, nd1, negator_1_out,
       negator_2_out, negator_3_out, oor, remu, slt, ssll, ssra, ssrl, ssub, subtractor_2_out, xxor;

  Adder #(.width(32)) adder_1 (.a(A), .b(B), .out(add));  // open: cin, cout
  Shifter #(.width(32), .shift("lr")) shifter_1 (.in(A), .\dist (B[4:0]), .out(ssrl));
  Shifter #(.width(32), .shift("ar")) shifter_2 (.in(A), .\dist (B[4:0]), .out(ssra));
  Shifter #(.width(32)) shifter_3 (.in(A), .\dist (B[4:0]), .out(ssll));
  Divider #(.width(32)) divider_1 (.a(A), .b(B), .out(divu), .rem(remu));  // open: upper
  Comparator #(.width(32)) comparator_1 (.a(A), .b(B), .lt(comparator_1_lt));  // open: gt, eq
  Subtractor #(.width(32)) subtractor_1 (.a(A), .b(B), .out(ssub));  // open: bin, bout
  assign nd1 = A & B;  // AND_Gate and_1, 32 bits wide
  assign oor = A | B;  // OR_Gate or_1, 32 bits wide
  assign xxor = A ^ B;  // XOR_Gate xor_1, 32 bits wide
  assign slt = {{31{1'b0}}, comparator_1_lt};  // Bit_Extender bit_extender_1
  Multiplier #(.width(32)) multiplier_1 (.a(A), .b(B), .out(mult), .cout(multhu));  // open: cin
  Multiplexer #(.select(4), .width(32), .enable("false")) multiplexer_1 (
    .in0(add), .in1(nd1), .in2(oor), .in3(xxor), .in4(ssrl), .in5(ssra), .in6(ssll), .in7(slt), .in8(divu),
    .in9(remu), .in10(mult), .in11(multhu), .in12(ssub), .in13(B), .in14(multiplexer_4_out), .out(Result),
    .sel(ALUSel));  // open: in15
  Negator #(.width(32)) negator_1 (.in(A), .out(negator_1_out));
  Negator #(.width(32)) negator_2 (.in(B), .out(negator_2_out));
  Multiplier #(.width(32)) multiplier_2 (.a(a1), .b(b1), .cout(multiplier_2_cout));  // open: out, cin
  Multiplexer #(.width(32), .enable("false")) multiplexer_2 (.in0(A), .in1(negator_1_out), .out(a1), .sel(A[31]));
  Multiplexer #(.width(32), .enable("false")) multiplexer_3 (.in0(B), .in1(negator_2_out), .out(b1), .sel(B[31]));
  xor xor_2 (m, A[31], B[31]);
  Negator #(.width(32)) negator_3 (.in(multiplier_2_cout), .out(negator_3_out));
  Subtractor #(.width(32)) subtractor_2 (.a(negator_3_out), .b(32'h1), .out(subtractor_2_out));  // open: bin, bout
  Multiplexer #(.width(32), .enable("false")) multiplexer_4 (
    .in0(multiplier_2_cout), .in1(subtractor_2_out), .out(multiplexer_4_out), .sel(m));

  // Other names for the same wires on the sheet: B5[4:0] = B[4:0]

  // Notes on the sheet:
  //   INPUTS to your circuit
  //   DON'T CHANGE THE LOCATIONS OF THE INPUTS AND OUTPUTS!
  //   OUTPUT from your circuit
endmodule
