// Logisim project control.circ as structural Verilog: 1 circuit, main circuit main
module main (
  output [2:0] ImmSel
);

  wire comparator_2_eq, comparator_3_eq, comparator_8_eq, Itype, or_1_out, Rtype, SBtype, Stype, UJtype,
       Utype;
  wire [6:0] opcode;

  Comparator #(.width(7)) comparator_1 (.a(opcode), .b(7'b0110011), .eq(Rtype));  // open: gt, lt
  Comparator #(.width(7)) comparator_2 (.a(opcode), .b(7'b0000011), .eq(comparator_2_eq));  // open: gt, lt
  Comparator #(.width(7)) comparator_3 (.a(opcode), .b(7'b0010011), .eq(comparator_3_eq));  // open: gt, lt
  Comparator #(.width(7)) comparator_4 (.a(opcode), .b(7'b0100011), .eq(Stype));  // open: gt, lt
  Comparator #(.width(7)) comparator_5 (.a(opcode), .b(7'b1100011), .eq(SBtype));  // open: gt, lt
  Comparator #(.width(7)) comparator_6 (.a(opcode), .b(7'b0110111), .eq(Utype));  // open: gt, lt
  Comparator #(.width(7)) comparator_7 (.a(opcode), .b(7'b1101111), .eq(UJtype));  // open: gt, lt
  Comparator #(.width(7)) comparator_8 (.a(opcode), .b(7'b1100111), .eq(comparator_8_eq));  // open: gt, lt
  or or_1 (or_1_out, comparator_2_eq, comparator_3_eq);
  or or_2 (Itype, or_1_out, comparator_8_eq);
  Multiplexer #(.select(5), .width(3), .enable("false")) multiplexer_1 (
    .in1(3'b000), .in2(3'b001), .in4(3'b010), .in8(3'b011), .in16(3'b100), .in31(3'b101), .out(ImmSel),
    .sel({UJtype, Utype, SBtype, Stype, Itype}));  // open: in0, in3, in5, in6, in7, in9, in10, in11, in12, in13, in14, in15, in17, in18, in19, in20, in21, in22, in23, in24, in25, in26, in27, in28, in29, in30
endmodule
