// Logisim project cpu.circ as structural Verilog: 5 circuits, main circuit main
module main (
  input  [31:0] INSTRUCTION,
  input  CLOCK,
  output [31:0] FETCH_ADDRESS,
  output [31:0] ra,
  output [31:0] sp,
  output [31:0] t0,
  output [31:0] t1,
  output [31:0] t2,
  output [31:0] s0,
  output [31:0] s1,
  output [31:0] a0
);

  wire ASel, BrEq, BrLt, BrUn, BSel, comparator_1_eq, DMEM_p1, DMEM_p7, DMEM_p9, DMEM_p12, DMEM_p14,
       DMEM_p16, lwc, MemRW, multiplexer_2_out, not_1_out, or_1_out, PCsel, pop, push, RegWEn;
  wire [1:0] WBSel;
  wire [2:0] funct3, ImmSel;
  wire [3:0] ALUSel;
  wire [4:0] R1, R2, RD, RDp;
  wire [6:0] funct7;
  wire [24:0] inst;
  wire [31:0] A, adder_4_out, ALU_A, ALU_B, ALUout, ALUoutLWC, B, DMEM_p11, Immediate, multiplexer_1_out,
       multiplexer_3_out, multiplexer_5_out, negator_1_out, pc, pc4, PROGRAM_COUNTER, sp4, spi, WriteBack,
       WriteBackpp;

  Adder #(.width(32)) adder_1 (.a(PROGRAM_COUNTER), .b(32'h4), .out(pc4));  // open: cin, cout
  Multiplexer #(.width(32), .enable("false")) multiplexer_1 (
    .in0(pc4), .in1(ALUout), .out(multiplexer_1_out), .sel(PCsel));
  Register #(.width(32)) u_PC (.D(multiplexer_1_out), .clk(CLOCK), .Q(PROGRAM_COUNTER));  // open: en, clr
  Comparator #(.width(32)) comparator_1 (.a(B), .b({32{1'b0}}), .eq(comparator_1_eq));  // open: gt, lt
  Shifter #(.width(32), .shift("lr")) shifter_1 (.in(PROGRAM_COUNTER), .\dist (5'b00010), .out(FETCH_ADDRESS));
  not not_1 (not_1_out, comparator_1_eq);
  control control_1 (
    .BrEq(BrEq), .BrLt(BrLt), .Instruction({funct7, inst[24:15], funct3, inst[11:0]}), .RD(RD), .BrUn(BrUn),
    .RS1(R1), .RS2(R2), .ALUsel(ALUSel), .ImmSel(ImmSel), .ASel(ASel), .BSel(BSel), .MemRW(MemRW),
    .RegWEn(RegWEn), .WBsel(WBSel), .PCsel(PCsel), .lwc(lwc), .push(push), .pop(pop));
  Multiplexer #(.enable("false")) multiplexer_2 (.in0(RegWEn), .in1(not_1_out), .out(multiplexer_2_out), .sel(lwc));
  Register #(.width(32)) register_1 (.D(PROGRAM_COUNTER), .clk(CLOCK), .Q(pc));  // open: en, clr
  Multiplexer #(.width(32), .enable("false")) multiplexer_3 (
    .in0(INSTRUCTION), .in1(32'h13), .out(multiplexer_3_out), .sel(PCsel));
  Negator #(.width(32)) negator_1 (.in(32'h4), .out(negator_1_out));
  Register #(.width(32)) register_2 (
    .D(multiplexer_3_out), .clk(CLOCK), .Q({funct7, inst[24:15], funct3, inst[11:0]}));  // open: en, clr
  Adder #(.width(32)) adder_2 (.a(sp), .b(negator_1_out), .out(sp4));  // open: cin, cout
  Multiplexer #(.width(5), .enable("false")) multiplexer_4 (.in0(RD), .in1(5'b00010), .out(RDp), .sel(or_1_out));
  or or_1 (or_1_out, push, pop);
  Multiplexer #(.width(32), .enable("false")) multiplexer_5 (
    .in0(WriteBack), .in1(sp4), .out(multiplexer_5_out), .sel(push));
  Multiplexer #(.width(32), .enable("false")) multiplexer_6 (
    .in0(multiplexer_5_out), .in1(spi), .out(WriteBackpp), .sel(pop));
  regfile_main RegFile (
    .rs2(R2), .rd(RDp), .Read_Data_1(A), .Read_Data_2(B), .ra(ra), .sp(sp), .t0(t0), .t1(t1), .t2(t2),
    .s0(s0), .s1(s1), .a0(a0), .rs1(R1), .Write_Data(WriteBackpp), .RegWEn(multiplexer_2_out), .clk(CLOCK));
  Adder #(.width(32)) adder_3 (.a(sp), .b(Immediate), .out(spi));  // open: cin, cout
  Multiplexer #(.width(32), .enable("false")) multiplexer_7 (.in0(pc), .in1(A), .out(ALU_A), .sel(ASel));
  Multiplexer #(.width(32), .enable("false")) multiplexer_8 (.in0(Immediate), .in1(B), .out(ALU_B), .sel(BSel));
  alu Arithmetic_Logic_Unit (.A(ALU_A), .B(ALU_B), .ALUSel(ALUSel), .Result(ALUout));
  immediate_generator immediate_generator_1 (
    .INSTRUCTION({funct7, inst[24:15], funct3, inst[11:0]}), .ImmSel(ImmSel), .Immediate(Immediate));
  Adder #(.width(32)) adder_4 (.a(A), .b(Immediate), .out(adder_4_out));  // open: cin, cout
  // mem_main DMEM: pin names not known; wires that end beside it: DMEM_p1, DMEM_p1, ALUoutLWC, B, MemRW, CLOCK, DMEM_p7, DMEM_p7, DMEM_p9, DMEM_p9, DMEM_p11, DMEM_p12, DMEM_p12, DMEM_p14, DMEM_p14, DMEM_p16
  branch_comp branch_comp_1 (.Data_A(A), .Data_B(B), .BrUn(BrUn), .BrEq(BrEq), .BrLt(BrLt));
  Multiplexer #(.width(32), .enable("false")) multiplexer_9 (
    .in0(ALUout), .in1(adder_4_out), .out(ALUoutLWC), .sel(lwc));
  Multiplexer #(.select(2), .width(32), .enable("false")) multiplexer_10 (
    .in0(ALUout), .in1(DMEM_p11), .in2(PROGRAM_COUNTER), .out(WriteBack), .sel(WBSel));  // open: in3

  // Other names for the same wires on the sheet: clk = CLOCK; opcode[6:0] = inst[6:0];
  //   inst (some bits) = {funct7, funct3}

  // Notes on the sheet:
  //   Output
  //   Inputs/Outputs from run.circ. DO NOT MOVE THESE.
  //   Inputs
  //   Inputs/Outputs from run.circ. DO NOT MOVE THESE.
endmodule

module immediate_generator (
  input  [31:0] INSTRUCTION,
  input  [2:0] ImmSel,
  output [31:0] Immediate
);

  wire [11:0] bit_extender_4_out;
  wire [19:0] bit_extender_3_out;
  wire [20:0] bit_extender_1_out, bit_extender_2_out;
  wire [31:0] bit_extender_5_out;

  assign bit_extender_1_out = {{20{INSTRUCTION[31]}}, INSTRUCTION[31]};  // Bit_Extender bit_extender_1
  assign bit_extender_2_out = {{20{INSTRUCTION[31]}}, INSTRUCTION[31]};  // Bit_Extender bit_extender_2
  assign bit_extender_3_out = {{19{INSTRUCTION[31]}}, INSTRUCTION[31]};  // Bit_Extender bit_extender_3
  assign bit_extender_4_out = {{11{INSTRUCTION[31]}}, INSTRUCTION[31]};  // Bit_Extender bit_extender_4
  assign bit_extender_5_out = {{25{1'b0}}, INSTRUCTION[31:25]};  // Bit_Extender bit_extender_5
  Multiplexer #(.select(3), .width(32), .enable("false")) multiplexer_1 (
    .in0({bit_extender_1_out, INSTRUCTION[30:20]}),
    .in1({bit_extender_2_out, INSTRUCTION[30:25], INSTRUCTION[11:7]}),
    .in2({bit_extender_3_out, INSTRUCTION[7], INSTRUCTION[30:25], INSTRUCTION[11:8], 1'b0}),
    .in3({INSTRUCTION[31:12], {12{1'b0}}}),
    .in4({bit_extender_4_out, INSTRUCTION[19:12], INSTRUCTION[20], INSTRUCTION[30:21], 1'b0}),
    .in5(bit_extender_5_out), .out(Immediate), .sel(ImmSel));  // open: in6, in7

  // Other names for the same wires on the sheet: funct7[6:0] = INSTRUCTION[31:25]; funct3[2:0] = INSTRUCTION[14:12];
  //   opcode[6:0] = INSTRUCTION[6:0]
endmodule

module control (
  input  BrEq,
  input  BrLt,
  input  [31:0] Instruction,
  output [4:0] RD,
  output BrUn,
  output [4:0] RS1,
  output [4:0] RS2,
  output [3:0] ALUsel,
  output [2:0] ImmSel,
  output ASel,
  output BSel,
  output MemRW,
  output RegWEn,
  output [1:0] WBsel,
  output PCsel,
  output lwc,
  output push,
  output pop
);

  wire and_2_out, and_3_out, and_4_out, and_5_out, BranchCode, comparator_2_eq, comparator_3_eq,
       comparator_8_eq, comparator_9_eq, comparator_10_eq, comparator_11_eq, comparator_12_eq,
       comparator_13_eq, comparator_14_eq, comparator_15_eq, comparator_16_eq, comparator_17_eq,
       comparator_18_eq, comparator_19_eq, comparator_20_eq, comparator_21_eq, comparator_22_eq,
       comparator_23_eq, comparator_24_eq, comparator_25_eq, Itype, not_2_out, or_1_out, or_4_out, or_5_out,
       or_6_out, or_9_out, or_10_out, or_11_out, SBtype, Stype, UJtype, Utype;
  wire [0:0] or_3_out;
  wire [1:0] bit_extender_1_out, bit_extender_2_out, multiplier_1_out;
  wire [4:0] multiplexer_1_out;

  alu_sel alu_sel_1 (.Instruction(Instruction), .ALU_sel(ALUsel));
  Comparator #(.width(7)) comparator_1 (.a(Instruction[6:0]), .b(7'b0110011), .eq(BSel));  // open: gt, lt
  Comparator #(.width(7)) comparator_2 (.a(Instruction[6:0]), .b(7'b0000011), .eq(comparator_2_eq));  // open: gt, lt
  Comparator #(.width(7)) comparator_3 (.a(Instruction[6:0]), .b(7'b0010011), .eq(comparator_3_eq));  // open: gt, lt
  Comparator #(.width(7)) comparator_4 (.a(Instruction[6:0]), .b(7'b0100011), .eq(Stype));  // open: gt, lt
  Comparator #(.width(7)) comparator_5 (.a(Instruction[6:0]), .b(7'b1100011), .eq(SBtype));  // open: gt, lt
  Comparator #(.width(7)) comparator_6 (.a(Instruction[6:0]), .b(7'b0110111), .eq(Utype));  // open: gt, lt
  Comparator #(.width(7)) comparator_7 (.a(Instruction[6:0]), .b(7'b1101111), .eq(UJtype));  // open: gt, lt
  Comparator #(.width(7)) comparator_8 (.a(Instruction[6:0]), .b(7'b1100111), .eq(comparator_8_eq));  // open: gt, lt
  or or_1 (or_1_out, comparator_2_eq, comparator_3_eq);
  or or_2 (Itype, or_1_out, comparator_8_eq);
  or or_3 (or_3_out[0], pop, Itype);
  Multiplexer #(.width(5), .enable("false")) multiplexer_1 (
    .in0({UJtype, Utype, SBtype, Stype, or_3_out[0]}), .in1({5{1'b0}}), .out(multiplexer_1_out), .sel(lwc));
  or or_4 (or_4_out, Stype, SBtype);
  Comparator #(.width(7)) comparator_9 (.a(Instruction[6:0]), .b(7'b1101111), .eq(comparator_9_eq));  // open: gt, lt
  Comparator #(.width(7)) comparator_10 (.a(Instruction[6:0]), .b(7'b1100111), .eq(comparator_10_eq));  // open: gt, lt
  not not_1 (RegWEn, or_4_out);
  Comparator #(.width(5)) comparator_11 (.a(Instruction[6:2]), .b({5{1'b0}}), .eq(comparator_11_eq));  // open: gt, lt
  Multiplexer #(.select(5), .width(3), .enable("false")) multiplexer_2 (
    .in0(3'b101), .in1(3'b000), .in2(3'b001), .in4(3'b010), .in8(3'b011), .in16(3'b100), .out(ImmSel),
    .sel(multiplexer_1_out));  // open: in3, in5, in6, in7, in9, in10, in11, in12, in13, in14, in15, in17, in18, in19, in20, in21, in22, in23, in24, in25, in26, in27, in28, in29, in30, in31
  or or_5 (or_5_out, Itype, Stype);
  or or_6 (or_6_out, comparator_9_eq, comparator_10_eq);
  or or_7 (ASel, BSel, or_5_out);
  or or_8 (MemRW, Stype, push);
  assign bit_extender_1_out = {{1{1'b0}}, comparator_11_eq};  // Bit_Extender bit_extender_1
  assign bit_extender_2_out = {{1{1'b0}}, or_6_out};  // Bit_Extender bit_extender_2
  Multiplier #(.width(2)) multiplier_1 (.a(2'b10), .b(bit_extender_2_out), .out(multiplier_1_out));  // open: cin, cout
  Adder #(.width(2)) adder_1 (.a(bit_extender_1_out), .b(multiplier_1_out), .out(WBsel));  // open: cin, cout
  and and_1 (BrUn, SBtype, Instruction[13]);
  Comparator #(.width(7)) comparator_12 (.a(Instruction[6:0]), .b(7'b0010011), .eq(comparator_12_eq));  // open: gt, lt
  Comparator #(.width(3)) comparator_13 (.a(Instruction[14:12]), .b(3'b000), .eq(comparator_13_eq));  // open: gt, lt
  Comparator #(.width(3)) comparator_14 (.a(Instruction[14:12]), .b(3'b100), .eq(comparator_14_eq));  // open: gt, lt
  Comparator #(.width(3)) comparator_15 (.a(Instruction[14:12]), .b(3'b110), .eq(comparator_15_eq));  // open: gt, lt
  Comparator #(.width(3)) comparator_16 (.a(Instruction[14:12]), .b(3'b001), .eq(comparator_16_eq));  // open: gt, lt
  not not_2 (not_2_out, BrEq);
  Comparator #(.width(7)) comparator_17 (.a(Instruction[6:0]), .b(7'b1101111), .eq(comparator_17_eq));  // open: gt, lt
  Comparator #(.width(7)) comparator_18 (.a(Instruction[6:0]), .b(7'b1100111), .eq(comparator_18_eq));  // open: gt, lt
  Comparator #(.width(7)) comparator_19 (.a(Instruction[6:0]), .b(7'b1100011), .eq(comparator_19_eq));  // open: gt, lt
  and and_2 (and_2_out, comparator_13_eq, BrEq);
  and and_3 (and_3_out, comparator_14_eq, BrLt);
  and and_4 (and_4_out, comparator_15_eq, BrLt);
  and and_5 (and_5_out, comparator_16_eq, not_2_out);
  or or_9 (or_9_out, comparator_17_eq, comparator_18_eq);
  Multiplexer #(.enable("false")) multiplexer_3 (.in0(or_9_out), .in1(BranchCode), .out(PCsel), .sel(comparator_19_eq));
  or or_10 (or_10_out, and_2_out, and_3_out);
  or or_11 (or_11_out, and_4_out, and_5_out);
  Comparator #(.width(7)) comparator_20 (.a(Instruction[6:0]), .b(7'b0000011), .eq(comparator_20_eq));  // open: gt, lt
  Comparator #(.width(3)) comparator_21 (.a(Instruction[14:12]), .b(3'b111), .eq(comparator_21_eq));  // open: gt, lt
  Comparator #(.width(7)) comparator_22 (.a(Instruction[6:0]), .b(7'b0111011), .eq(comparator_22_eq));  // open: gt, lt
  Comparator #(.width(3)) comparator_23 (.a(Instruction[14:12]), .b(3'b011), .eq(comparator_23_eq));  // open: gt, lt
  Comparator #(.width(7)) comparator_24 (.a(Instruction[6:0]), .b(7'b0111011), .eq(comparator_24_eq));  // open: gt, lt
  Comparator #(.width(3)) comparator_25 (.a(Instruction[14:12]), .b(3'b010), .eq(comparator_25_eq));  // open: gt, lt
  or or_12 (BranchCode, or_10_out, or_11_out);
  and and_6 (lwc, comparator_20_eq, comparator_21_eq);
  and and_7 (push, comparator_22_eq, comparator_23_eq);
  and and_8 (pop, comparator_24_eq, comparator_25_eq);

  assign RD = Instruction[11:7];
  assign RS1 = Instruction[19:15];
  assign RS2 = Instruction[24:20];

  // Other names for the same wires on the sheet: opcode[6:0] = Instruction[6:0]; funct3[2:0] = Instruction[14:12];
  //   funct7[6:0] = Instruction[31:25]; pc = PCsel; Rtype = BSel

  // Notes on the sheet:
  //   0=ALU
  //   1=mem
  //   2=pc+4
  //   1=reg
  //   1=write
endmodule

module branch_comp (
  input  [31:0] Data_A,
  input  [31:0] Data_B,
  input  BrUn,
  output BrEq,
  output BrLt
);

  wire comparator_1_eq, comparator_1_lt, comparator_2_eq, comparator_2_lt;

  Comparator #(.width(32)) comparator_1 (
    .a(Data_A), .b(Data_B), .eq(comparator_1_eq), .lt(comparator_1_lt));  // open: gt
  Comparator #(.width(32), .mode("unsigned")) comparator_2 (
    .a(Data_A), .b(Data_B), .eq(comparator_2_eq), .lt(comparator_2_lt));  // open: gt
  Multiplexer #(.enable("false")) multiplexer_1 (.in0(comparator_1_eq), .in1(comparator_2_eq), .out(BrEq), .sel(BrUn));
  Multiplexer #(.enable("false")) multiplexer_2 (.in0(comparator_1_lt), .in1(comparator_2_lt), .out(BrLt), .sel(BrUn));
endmodule

module alu_sel (
  input  [31:0] Instruction,
  output [3:0] ALU_sel
);

  wire and_1_out, comparator_6_eq, comparator_7_eq, comparator_8_eq;
  wire [1:0] c7, comparator_1_eq;
  wire [2:0] comparator_3_eq;
  wire [3:0] AMS, comparator_9_eq, DSS, I_code, multiplexer_1_out, multiplexer_8_out, multiplexer_9_out,
       R_code, RA, SM;

  Comparator #(.width(7)) comparator_1 (.a(Instruction[6:0]), .b(7'b0010011), .eq(comparator_1_eq[0]));  // open: gt, lt
  Comparator #(.width(7)) comparator_2 (.a(Instruction[6:0]), .b(7'b0110011), .eq(comparator_1_eq[1]));  // open: gt, lt
  Comparator #(.width(7)) comparator_3 (
    .a(Instruction[31:25]), .b({7{1'b0}}), .eq(comparator_3_eq[0]));  // open: gt, lt
  Comparator #(.width(7)) comparator_4 (
    .a(Instruction[31:25]), .b(7'b0000001), .eq(comparator_3_eq[1]));  // open: gt, lt
  Comparator #(.width(7)) comparator_5 (
    .a(Instruction[31:25]), .b(7'b0100000), .eq(comparator_3_eq[2]));  // open: gt, lt
  Multiplexer #(.select(2), .width(4), .enable("false")) multiplexer_1 (
    .in0(4'b0000), .in1(I_code), .in2(R_code), .out(multiplexer_1_out), .sel(comparator_1_eq));  // open: in3
  Comparator #(.width(7)) comparator_6 (.a(Instruction[6:0]), .b(7'b0110111), .eq(comparator_6_eq));  // open: gt, lt
  Multiplexer #(.select(3), .width(2), .enable("false")) multiplexer_2 (
    .in1(2'b00), .in2(2'b01), .in4(2'b10), .out(c7), .sel(comparator_3_eq));  // open: in0, in3, in5, in6, in7
  Multiplexer #(.width(4), .enable("false")) multiplexer_3 (
    .in0(multiplexer_1_out), .in1(4'b1101), .out(ALU_sel), .sel(comparator_6_eq));
  Multiplexer #(.select(2), .width(4), .enable("false")) multiplexer_4 (
    .in0(4'b0000), .in1(4'b1010), .in2(4'b1100), .out(AMS), .sel(c7));  // open: in3
  Multiplexer #(.select(2), .width(4), .enable("false")) multiplexer_5 (
    .in0(4'b0110), .in1(4'b1011), .out(SM), .sel(c7));  // open: in2, in3
  Multiplexer #(.select(2), .width(4), .enable("false")) multiplexer_6 (
    .in0(4'b0100), .in1(4'b1000), .in2(4'b0101), .out(DSS), .sel(c7));  // open: in3
  Multiplexer #(.select(2), .width(4), .enable("false")) multiplexer_7 (
    .in0(4'b0001), .in1(4'b1001), .out(RA), .sel(c7));  // open: in2, in3
  Multiplexer #(.select(3), .width(4), .enable("false")) multiplexer_8 (
    .in0(4'b0000), .in1(4'b0110), .in2(4'b0111), .in4(4'b0011), .in5(4'b0101), .in6(4'b0010), .in7(4'b0001),
    .out(multiplexer_8_out), .sel(Instruction[14:12]));  // open: in3
  Multiplexer #(.select(3), .width(4), .enable("false")) multiplexer_9 (
    .in0(4'b0000), .in1(4'b0110), .in2(4'b0111), .in3(4'b1011), .in4(4'b0011), .in5(4'b0101), .in6(4'b0010),
    .in7(4'b0001), .out(multiplexer_9_out), .sel(Instruction[14:12]));
  Comparator #(.width(4)) comparator_7 (.a(multiplexer_8_out), .b(4'b0101), .eq(comparator_7_eq));  // open: gt, lt
  Comparator #(.width(7)) comparator_8 (.a(Instruction[31:25]), .b({7{1'b0}}), .eq(comparator_8_eq));  // open: gt, lt
  Multiplexer #(.width(4), .enable("false")) multiplexer_10 (
    .in0(multiplexer_8_out), .in1(4'b0100), .out(I_code), .sel(and_1_out));
  and and_1 (and_1_out, comparator_7_eq, comparator_8_eq);
  Comparator #(.width(4)) comparator_9 (.a(multiplexer_9_out), .b(4'b0000), .eq(comparator_9_eq[0]));  // open: gt, lt
  Comparator #(.width(4)) comparator_10 (.a(multiplexer_9_out), .b(4'b0110), .eq(comparator_9_eq[1]));  // open: gt, lt
  Comparator #(.width(4)) comparator_11 (.a(multiplexer_9_out), .b(4'b0101), .eq(comparator_9_eq[2]));  // open: gt, lt
  Comparator #(.width(4)) comparator_12 (.a(multiplexer_9_out), .b(4'b0001), .eq(comparator_9_eq[3]));  // open: gt, lt
  Multiplexer #(.select(4), .width(4), .enable("false")) multiplexer_11 (
    .in0(multiplexer_9_out), .in1(AMS), .in2(SM), .in4(DSS), .in8(RA), .out(R_code), .sel(comparator_9_eq));  // open: in3, in5, in6, in7, in9, in10, in11, in12, in13, in14, in15

  // Other names for the same wires on the sheet: opcode[6:0] = Instruction[6:0]; funct3[2:0] = Instruction[14:12];
  //   funct7[6:0] = Instruction[31:25]

  // Notes on the sheet:
  //   sll, mulh
  //   divu,srl,sra
  //   remu,and
  //   add, mul, sub
endmodule
