// Logisim project CPU-swlw.circ as structural Verilog: 1 circuit, main circuit main
module main (
  output [31:0] ra,
  output [31:0] sp,
  output [31:0] t0,
  output [31:0] t1,
  output [31:0] t2,
  output [31:0] s0,
  output [31:0] s1,
  output [31:0] a0,
  output [31:0] Requested_Address,
  output [31:0] Requested_Instruction,
  output [15:0] Time_Step,
  output halt
);

  wire clk;

  Clock clock_1 (.out(clk));
  // Probe on Requested_Address
  ROM #(.addrWidth(14), .dataWidth(32)) rom_1 (.addr(Requested_Address[13:0]), .data(Requested_Instruction));
  cpu_main main_1 (
    .INSTRUCTION(Requested_Instruction), .CLOCK(clk), .ra(ra), .sp(sp), .t0(t0), .t1(t1), .t2(t2), .s0(s0),
    .s1(s1), .a0(a0), .FETCH_ADDRESS(Requested_Address));
  // Probe on Requested_Instruction
  Counter #(.width(16), .max('hffff)) counter_1 (.clk(clk), .Q(Time_Step));  // open: clr, load, up, count, D, carry
  Comparator #(.width(16)) comparator_1 (.a(Time_Step), .b(16'h6fc), .eq(halt));  // open: gt, lt

  // Other names for the same wires on the sheet: fetch_addr[31:0] = Requested_Address;
  //   Instruction[31:0] = Requested_Instruction

  // Notes on the sheet:
  //   contents of rom_1 (hex, n*v repeats v):
  //   06450093 06450113 06450293 06450313 06450393 06450413 06450493 06450513 00850513 01609093 0180A093
  //   0054C493 01D15113 40F45413 0004E493 01247413 00350513 01741413 00F4A493 01E14113 00355513 41055513
  //   01C16113 0080F093 00C48493 00B11113 00B12113 00854513 01D35313 40A4D493 0102E293 00F3F393 01850513
  //   01949493 0122A293 00754513 00755513 40715113 00316113 0144F493 01A10113 00B49493 0082A293 00F0C093
  //   01C55513 4193D393 01A0E093 00E0F093 00930313 00A09093 00152513 00A34313 00845413 40535313 01046413
  //   0012F293 00B48493 00049493 01112113 0054C493 01315113 41515113 0040E093 0080F093 00740413 01039393
  //   00D42413 0172C293 01345413 41155513 01E36313 00957513 00E50513 01E41413 0142A293 01444413 0134D493
  //   41315113 00436313 01F0F093 00E40413 00609093 00F0A093 0144C493 01815113 41935313 00B56513 01017113
  //   00C10113 00511113 0164A493 0173C393 01355513 40F2D293 0144E493 0184F493 00C48493 01139393 01642413
  //   0150C093 00C35313 4130D093 0000E093 01D3F393 01A40413 01229293 00B3A393 0190C093 0110D093 41C15113
  //   00146413 00D3F393 01C08093 00A41413 0020A093 00914113 0160D093 40115113 01816113 0033F393 01930313
  //   01B49493 01912113 01A4C493 0180D093 40B4D493 01746413 01B17113 01A48493 01451513 01A4A493 01744413
  //   00655513 4170D093 01936313 0052F293 01E08093 01411113 00B0A093 0004C493 0194D493 40A45413 0134E493
  //   0152F293 01B10113 00109093 0162A293 00D3C393 00B55513 4073D393 01D46413 00937313 00B08093 00B39393
  //   00B2A293 00954513 01635313 40555513 0134E493 00F17113 00C10113 00749493 01B32313 01B44413 01555513
  //   41015113 00846413 00D17113 00250513 01F49493 0073A393 01854513 01035313 40115113 00256513 0010F093
  //   00830313 00651513 0072A293 0084C493 01B55513 40545413 01E4E493 01A0F093 01B38393 01331313 00C4A493
  //   0152C293 0103D393 4082D293 00E36313 01137313 01A38393 01949493 01752513 00E4C493 00635313 40E35313
  //   00A3E393 00947413 00B28293 00D39393 0012A293 00534313 01345413 4022D293 0110E093 01347413 00440413
  //   01939393 0063A393 01214113 0033D393 41115113 0003E393 01D57513 00510113 01309093 01632313 0082C293
  //   0102D293 4142D293 00A3E393 00C0F093 01730313 00F29293 01042413 00334313 01945413 4192D293 01546413
  //   0150F093 01F40413 00031313 01C4A493 01A34313 01C4D493 41155513 00016113 00B47413 00410113 01129293
  //   01752513 00E54513 01255513 40615113 01B3E393 01317113 00538393 00C39393 00C12113 00C0C093 00F3D393
  //   4123D393 0024E493 00657513 01640413 01729293 01A0A093 0084C493 00F55513 41615113 01C2E293 0123F393
  //   00C50513 00E09093 0113A393 00F3C393 00615113 41315113 0092E293 00B4F493 00D08093 01941413 01A2A293
  //   00244413 0000D093 4033D393 00D3E393 0180F093 00230313 01551513 00E32313 01E14113 0014D493 40B35313
  //   0150E093 01E47413 01728293 01751513 01C42413 00F34313 00D4D493 40E3D393 01816113 01A4F493 01248493
  //   01729293 0030A093 00C4C493 0014D493 40045413 01316113 0033F393 00D08093 01C41413 0132A293 0043C393
  //   01455513 4020D093 00216113 01A0F093 00510113 01511113 01F32313 00A14113 0052D293 40D0D093 01856513
  //   00B17113 01A48493 00A49493 00C12113 0180C093 01D15113 40755513 01D56513 00E4F493 00128293 01F29293
  //   00952513 01144413 0050D093 4124D493 00746413 00817113 01310113 01051513 0053A393 00A3C393 00845413
  //   40B15113 0093E393 0093F393 01448493 00131313 0082A293 00244413 00835313 41135313 00B16113 00B4F493
  //   00330313 01A49493 01B4A493 00244413 0084D493 41C0D093 0132E293 01557513 01250513 01331313 01B12113
  //   0130C093 01A2D293 4104D493 0044E493 0143F393 00C08093 00B29293 00A0A093 01A34313 00335313 41545413
  //   01B36313 0012F293 01208093 00129293 00842413 00F4C493 00455513 40E3D393 01C2E293 00C37313 01748493
  //   01D11113 0070A093 0050C093 0183D393 40315113 0170E093 01D0F093 01628293 01831313 0020A093 00E44413
  //   01A2D293 40045413 0110E093 00B2F293 01340413 00551513 0033A393 01134313 0094D493 4104D493 01A0E093
  //   00447413 00C38393 00829293 0103A393 0052C293 00F4D493 41445413 01156513 01247413 00F38393 01041413
  //   01242413 01834313 00F35313 41545413 00C3E393 01137313 01E40413 01D09093 01212113 01654513 00345413
  //   4092D293 0004E493 0073F393 01C48493 01E31313 01712113 00444413 00D0D093 40E0D093 0040E093 01A47413
  //   00D40413 00929293 01D52513 01134313 00D4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
  //   Instruction Memory
  //   YOUR CPU SHOULD FIT IN HERE!
  //   Halts Execution After Constant # of Clock Cycles
  //   Constant
endmodule
