// Logisim project CPU-tricky.circ as structural Verilog: 1 circuit, main circuit main
module main (
  output [31:0] ra,
  output [31:0] sp,
  output [31:0] t0,
  output [31:0] t1,
  output [31:0] t2,
  output [31:0] s0,
  output [31:0] s1,
  output [31:0] a0,
  output [31:0] Requested_Address,
  output [31:0] Requested_Instruction,
  output [15:0] Time_Step,
  output halt
);

  wire clk;

  Clock clock_1 (.out(clk));
  // Probe on Requested_Address
  ROM #(.addrWidth(14), .dataWidth(32)) rom_1 (.addr(Requested_Address[13:0]), .data(Requested_Instruction));
  cpu_main main_1 (
    .INSTRUCTION(Requested_Instruction), .CLOCK(clk), .ra(ra), .sp(sp), .t0(t0), .t1(t1), .t2(t2), .s0(s0),
    .s1(s1), .a0(a0), .FETCH_ADDRESS(Requested_Address));
  // Probe on Requested_Instruction
  Counter #(.width(16), .max('hffff)) counter_1 (.clk(clk), .Q(Time_Step));  // open: clr, load, up, count, D, carry
  Comparator #(.width(16)) comparator_1 (.a(Time_Step), .b(16'h909), .eq(halt));  // open: gt, lt

  // Other names for the same wires on the sheet: fetch_addr[31:0] = Requested_Address;
  //   Instruction[31:0] = Requested_Instruction

  // Notes on the sheet:
  //   contents of rom_1 (hex, n*v repeats v):
  //   00150093 00150113 00150293 00150313 00150393 00150413 00150493 00150513 002114B3 02153133 0023D133
  //   002504B3 0252B533 00929333 00154533 40938533 00716333 008562B3 00944433 021394B3 00A4F0B3 00945533
  //   0022D133 00210533 001103B3 00948333 0050A333 002492B3 00646533 00239333 00A122B3 00A57433 007323B3
  //   00844533 007300B3 0080F133 00951133 00850433 007163B3 0213B333 0072A0B3 0093D2B3 40540133 4070D0B3
  //   028313B3 0022F2B3 00A30333 009290B3 0074F3B3 00612533 0070E433 00608533 00210433 005383B3 00830433
  //   02808533 00A0A4B3 00A50133 00609433 005280B3 002080B3 00A373B3 00938333 00148433 02848133 02841133
  //   006283B3 00138333 0053C533 406083B3 009514B3 00528533 40930333 00657433 02A51433 00640133 00712433
  //   405082B3 005090B3 026102B3 005492B3 00730533 002140B3 00808133 00531333 0063F3B3 00A0F4B3 40930133
  //   027503B3 02A40133 00A30333 006363B3 022393B3 00940433 002473B3 0014E133 002353B3 00828433 005502B3
  //   002490B3 002402B3 007144B3 00932433 027514B3 001280B3 00A4F0B3 005422B3 00850433 006484B3 40A50433
  //   0060C4B3 00738133 00910533 0052E4B3 00A3C2B3 009454B3 00110133 0054D4B3 40555433 00550533 00514533
  //   409352B3 0083C3B3 009280B3 4080D2B3 00946133 0264B533 00A10433 00629433 02110333 0010C533 00547533
  //   0274B433 02629433 00130433 00840333 40828333 00245533 00956433 00240133 0063A2B3 00A16133 022414B3
  //   408104B3 0282B4B3 0260B2B3 0084F3B3 4080D3B3 00A383B3 008403B3 001382B3 02729333 021530B3 4050D433
  //   0210B3B3 4012D533 00257433 006124B3 0074D3B3 0080D0B3 40A152B3 022113B3 00751433 00211133 005450B3
  //   005410B3 40A50433 00639333 001403B3 00A382B3 00614333 00710333 026402B3 002382B3 401400B3 026280B3
  //   4074D4B3 40908433 0073D4B3 00A14433 00930333 00236533 4010D3B3 0010E2B3 02628433 00955333 02750333
  //   40610133 007340B3 001373B3 002373B3 00528433 02A383B3 00531533 0023E333 0093A333 00A082B3 005422B3
  //   009300B3 02748533 027310B3 00A502B3 0092C3B3 006520B3 0290B433 4053D533 0283B333 02813433 40945133
  //   00728433 00809533 001302B3 02548333 00148333 0050F2B3 0083F2B3 006083B3 401484B3 0012C533 001480B3
  //   006440B3 02A41533 0080D133 0292B433 00A38533 0064F433 406282B3 002350B3 008402B3 00A0D133 002303B3
  //   029133B3 00139533 02628533 00A0A0B3 0024E533 00A08333 02230133 02A494B3 40A104B3 007553B3 00937133
  //   00938133 0083E2B3 0012A433 007472B3 00915533 005473B3 00817333 00640133 0010E3B3 00938533 02833133
  //   008303B3 00532433 02913133 00751433 00A080B3 40238333 029430B3 40A450B3 007154B3 40240133 02153433
  //   005084B3 009283B3 408150B3 0212B3B3 00538433 001463B3 02729133 00A48133 00A4C533 029283B3 4082D2B3
  //   409102B3 0073F533 027392B3 00845533 4093D4B3 00110333 00110433 001280B3 00748533 002100B3 00A2F3B3
  //   0084E2B3 4054D2B3 40238433 027083B3 0010A533 0083D2B3 0014E333 001554B3 00915333 40710333 028490B3
  //   00A3F4B3 002304B3 00A0A133 40A300B3 00712133 0084D133 007292B3 4013D433 021502B3 00541133 401280B3
  //   00A38133 0053E0B3 02213433 009284B3 005564B3 02840133 005480B3 4014D433 40928133 007454B3 402482B3
  //   002524B3 02250533 00631533 0070C3B3 0012A433 02111133 00831133 006154B3 009403B3 002482B3 02A51133
  //   00637133 40A28333 028402B3 0264B2B3 401454B3 0083A333 008310B3 40608333 005503B3 00850533 00A4A333
  //   02948133 0084E0B3 405282B3 0094D3B3 009090B3 02509333 00255433 0290B4B3 00808433 025430B3 001474B3
  //   00654333 02839433 00844433 4014D3B3 00640333 40840133 00A094B3 008084B3 0092A333 008463B3 007080B3
  //   4014D2B3 0022D333 00808533 0050D2B3 008370B3 401152B3 0212B533 00A2C333 0060D0B3 00228433 001482B3
  //   02A393B3 00708433 0050A0B3 00155333 408400B3 021403B3 007103B3 00928333 00848333 0022D2B3 02943533
  //   00616433 406552B3 00917433 009394B3 0073C3B3 00930533 02250133 009102B3 0264B4B3 02A29333 00240333
  //   008102B3 0020C0B3 407283B3 40530333 0270B2B3 0064A4B3 00946433 00A360B3 0250B133 00A4E3B3 006340B3
  //   006174B3 006382B3 029534B3 0024D4B3 001292B3 0022C133 0053A2B3 028333B3 02513533 0024D3B3 0020C0B3
  //   02A39333 022334B3 0020C0B3 40810533 0070D0B3 025302B3 0050A3B3 0092D533 02151333 008514B3 001310B3
  //   40738333 00140533 005484B3 029280B3 008514B3 0023A333 00948133 026084B3 02738433 02951133 001550B3
  //   00217333 00A454B3 009300B3 006503B3 0293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
  //   Instruction Memory
  //   YOUR CPU SHOULD FIT IN HERE!
  //   Halts Execution After Constant # of Clock Cycles
  //   Constant
endmodule
